# Fritzing sketch rotocalco_blackDot (saved by Fritzing 0.9.3b)

parts:
  R2 = Photocell (LDR) [package=THT]
  WHITE_LED = LED - 5mm [color="White (6500K)" package="5 mm [THT]"]
  R1 = Resistor [tolerance=±5% resistance=100 package=THT]
  R3 = Resistor [tolerance=±5% resistance=10k package=THT]
  R4 = Rotary Potentiometer (Small) [maximum_resistance=10kΩ package=THT]  # not connected
  R4_2 = Trimmer Potentiometer [maximum_resistance=10kΩ package=THT]  # not connected
  LED1 = LED - 5mm [color="Red (633nm)" package="5 mm [THT]"]  # not connected
  R5 = Resistor [tolerance=±5% resistance=220 package=THT]  # not connected

nets:
  N1: R2.pin_0, R3.Pin_0
  N2: R2.pin_1, WHITE_LED.cathode
  N3: WHITE_LED.anode, R1.Pin_1
